// Logisim project alu (1).circ as structural Verilog: 1 circuit, main circuit main
module main (
  input  in_1,
  input  in_2,
  input  in_3,
  input  in_4,
  input  in_5,
  input  in_6,
  input  in_7,
  input  in_8,
  input  in_9,
  input  in_10,
  input  in_11,
  output out_12,
  output out_13,
  output out_14,
  output out_15
);

  wire ADD_0, ADD_1, ADD_2, ADD_2_out, ADD_3, ADD_3_out, ADD_4_out, ADD_out, AND_0, AND_1, AND_2, AND_3,
       and_5_out, and_6_out, and_7_out, and_8_out, and_9_out, and_10_out, AND_11_out, AND_12_out, AND_13_out,
       AND_14_out, G0_out, G1_out, G2_out, NOT_0, NOT_1, NOT_2, NOT_3, not_5_out, not_6_out, not_7_out,
       not_8_out, not_9_out, not_10_out, not_11_out, not_12_out, NOT_13_out, NOT_14_out, NOT_15_out,
       NOT_16_out, OR_0, OR_1, OR_2, OR_3, or_5_out, or_6_out, or_7_out, OR_8_out, OR_9_out, OR_10_out,
       OR_11_out, P0_out, P1_out, P2_out, P3_out;

  not u_not_1 (NOT_0, in_8);
  not u_not_2 (NOT_1, in_7);
  not u_not_3 (NOT_2, in_6);
  not not_4 (NOT_3, in_5);
  or u_or_1 (OR_0, in_8, in_4);
  or u_or_2 (OR_1, in_7, in_3);
  or u_or_3 (OR_2, in_6, in_2);
  or or_4 (OR_3, in_5, in_1);
  and u_and_1 (AND_0, in_8, in_4);
  and u_and_2 (AND_1, in_7, in_3);
  and u_and_3 (AND_2, in_6, in_2);
  and and_4 (AND_3, in_5, in_1);
  xor P0 (P0_out, in_8, in_4);
  and G0 (G0_out, in_8, in_4);
  xor P1 (P1_out, in_7, in_3);
  and G1 (G1_out, in_7, in_3);
  xor P2 (P2_out, in_6, in_2);
  and G2 (G2_out, in_6, in_2);
  xor P3 (P3_out, in_5, in_1);
  // AND_Gate G3 has open pins: in0=in_5, in1=in_1, out=open
  and and_5 (and_5_out, G0_out, P2_out);
  and and_6 (and_6_out, G0_out, P1_out);
  and and_7 (and_7_out, in_11, P0_out, P1_out);
  and and_8 (and_8_out, in_11, P0_out, G1_out, P2_out);
  or or_5 (or_5_out, G0_out, and_9_out);
  and and_9 (and_9_out, P0_out, in_11);
  and and_10 (and_10_out, G1_out, P2_out);
  not not_5 (not_5_out, in_9);
  not not_6 (not_6_out, in_10);
  not not_7 (not_7_out, in_9);
  not not_8 (not_8_out, in_10);
  or or_6 (or_6_out, G1_out, and_6_out, and_7_out);
  or or_7 (or_7_out, G2_out, and_10_out, and_5_out, and_8_out);
  not not_9 (not_9_out, in_9);
  not not_10 (not_10_out, in_10);
  not not_11 (not_11_out, in_9);
  not not_12 (not_12_out, in_10);
  xor xor_1 (ADD_0, in_11, P0_out);
  xor xor_2 (ADD_1, or_5_out, P1_out);
  xor xor_3 (ADD_2, or_6_out, P2_out);
  xor xor_4 (ADD_3, or_7_out, P3_out);
  and NOT_13 (NOT_13_out, not_9_out, NOT_0, not_10_out);
  and OR_8 (OR_8_out, not_9_out, OR_0, in_10);
  and AND_11 (AND_11_out, in_9, AND_0, not_10_out);
  and ADD (ADD_out, in_9, ADD_0, in_10);
  and NOT_14 (NOT_14_out, not_11_out, NOT_1, not_12_out);
  and OR_9 (OR_9_out, not_11_out, OR_1, in_10);
  and AND_12 (AND_12_out, in_9, AND_1, not_12_out);
  and u_ADD_2 (ADD_2_out, in_9, ADD_1, in_10);
  and NOT_15 (NOT_15_out, not_5_out, NOT_2, not_6_out);
  and OR_10 (OR_10_out, not_5_out, OR_2, in_10);
  and AND_13 (AND_13_out, in_9, AND_2, not_6_out);
  and u_ADD_3 (ADD_3_out, in_9, ADD_2, in_10);
  and NOT_16 (NOT_16_out, not_7_out, NOT_3, not_8_out);
  and OR_11 (OR_11_out, not_7_out, OR_3, in_10);
  and AND_14 (AND_14_out, in_9, AND_3, not_8_out);
  and ADD_4 (ADD_4_out, in_9, ADD_3, in_10);
  or or_12 (out_14, NOT_14_out, OR_9_out, AND_12_out, ADD_2_out);
  or or_13 (out_13, NOT_15_out, OR_10_out, AND_13_out, ADD_3_out);
  or or_14 (out_12, NOT_16_out, OR_11_out, AND_14_out, ADD_4_out);
  or or_15 (out_15, NOT_13_out, OR_8_out, AND_11_out, ADD_out);

  // Other names for the same wires on the sheet: A0 = in_8; A1 = in_7; A2 = in_6; A3 = in_5; B0 = in_4; B1 = in_3;
  //   B2 = in_2; B3 = in_1; C0 = out_15; C1 = out_14; C2 = out_13; C3 = out_12; CIN = in_11; S0 = in_10; S1 = in_9
endmodule
