// Logisim project hw1p2.circ as structural Verilog: 1 circuit, main circuit main
module main (
  input  bit_1,
  input  in_2,
  input  in_3,
  input  in_4,
  input  bit_5,
  output out_6,
  output out_7,
  output out_8
);

  wire and_1_out, and_2_out, and_3_out, and_4_out, and_5_out, and_6_out, and_7_out, and_8_out, and_9_out,
       and_10_out, and_11_out, and_12_out, and_13_out, and_14_out, and_15_out, and_16_out, and_17_out,
       and_18_out, and_19_out, and_20_out, and_21_out, and_22_out, and_23_out, and_24_out, and_25_out,
       and_26_out, and_27_out, and_28_out, and_29_out, and_30_out, and_31_out, not_1_out, not_2_out,
       not_3_out, not_4_out, not_5_out;

  not not_1 (not_1_out, bit_1);
  not not_2 (not_2_out, in_2);
  not not_3 (not_3_out, in_3);
  not not_4 (not_4_out, in_4);
  not not_5 (not_5_out, bit_5);
  and and_1 (and_1_out, bit_1, in_2, in_3, in_4);
  and and_2 (and_2_out, bit_1, in_2, in_3, bit_5);
  and and_3 (and_3_out, bit_1, in_2, in_4, bit_5);
  and and_4 (and_4_out, bit_1, in_3, in_4, bit_5);
  and and_5 (and_5_out, in_2, in_3, in_4, bit_5);
  and and_6 (and_6_out, bit_1, in_2, not_3_out, not_4_out);
  and and_7 (and_7_out, bit_1, not_2_out, in_3, not_4_out);
  and and_8 (and_8_out, bit_1, not_2_out, not_3_out, in_4);
  and and_9 (and_9_out, bit_1, not_2_out, not_3_out, bit_5);
  and and_10 (and_10_out, in_2, in_3, not_4_out, not_5_out);
  and and_11 (and_11_out, in_2, not_3_out, in_4, not_5_out);
  and and_12 (and_12_out, not_1_out, in_2, not_3_out, bit_5);
  and and_13 (and_13_out, not_1_out, in_3, in_4, not_5_out);
  and and_14 (and_14_out, not_1_out, in_3, not_4_out, bit_5);
  and and_15 (and_15_out, not_1_out, not_2_out, in_4, bit_5);
  and and_16 (and_16_out, not_1_out, not_2_out, not_3_out, not_4_out, bit_5);
  and and_17 (and_17_out, not_1_out, not_2_out, not_3_out, in_4, not_5_out);
  and and_18 (and_18_out, not_1_out, not_2_out, in_3, not_4_out, not_5_out);
  and and_19 (and_19_out, not_1_out, not_2_out, in_3, in_4, bit_5);
  and and_20 (and_20_out, not_1_out, in_2, not_3_out, not_4_out, not_5_out);
  and and_21 (and_21_out, not_1_out, in_2, not_3_out, in_4, bit_5);
  and and_22 (and_22_out, not_1_out, in_2, in_3, not_4_out, bit_5);
  and and_23 (and_23_out, not_1_out, in_2, in_3, in_4, not_5_out);
  and and_24 (and_24_out, bit_1, not_2_out, not_3_out, not_4_out, not_5_out);
  and and_25 (and_25_out, bit_1, not_2_out, not_3_out, in_4, bit_5);
  and and_26 (and_26_out, bit_1, not_2_out, in_3, not_4_out, bit_5);
  and and_27 (and_27_out, bit_1, not_2_out, in_3, in_4, not_5_out);
  and and_28 (and_28_out, bit_1, in_2, not_3_out, not_4_out, bit_5);
  and and_29 (and_29_out, bit_1, in_2, not_3_out, in_4, not_5_out);
  and and_30 (and_30_out, bit_1, in_2, in_3, not_4_out, not_5_out);
  and and_31 (and_31_out, bit_1, in_2, in_3, in_4, bit_5);
  or or_1 (out_6, and_1_out, and_2_out, and_3_out, and_4_out, and_5_out);
  or or_2 (out_7, and_6_out, and_7_out, and_8_out, and_9_out, and_10_out, and_11_out, and_12_out, and_13_out, and_14_out, and_15_out);
  or or_3 (out_8, and_16_out, and_17_out, and_18_out, and_19_out, and_20_out, and_21_out, and_22_out, and_23_out, and_24_out, and_25_out, and_26_out, and_27_out, and_28_out, and_29_out, and_30_out, and_31_out);

  // Other names for the same wires on the sheet: output_bit_1 = out_8; output_bit_2 = out_7; output_bit_3 = out_6
endmodule
