// Logisim project logisim 3.circ as structural Verilog: 1 circuit, main circuit main
module main (
  input  in_1,
  input  in_2,
  input  in_3,
  input  in_4
);

  wire and_1_out, and_2_out, and_3_out, and_4_out, and_5_out, and_6_out, and_7_out, and_8_out, and_9_out,
       and_10_out, and_11_out, and_12_out, and_13_out, and_14_out, and_15_out, c0_out, c1_out, c2_out,
       c3_out, c4_out, c5_out, c6_out, not_1_out, not_2_out, not_3_out, not_4_out;

  not not_1 (not_1_out, in_1);
  not not_2 (not_2_out, in_2);
  not not_3 (not_3_out, in_3);
  not not_4 (not_4_out, in_4);
  buf and_1 (and_1_out, in_1);  // AND_Gate
  and and_2 (and_2_out, in_2, in_4);
  buf and_3 (and_3_out, in_3);  // AND_Gate
  and and_4 (and_4_out, not_2_out, not_4_out);
  and and_5 (and_5_out, not_3_out, not_4_out);
  and and_6 (and_6_out, in_3, in_4);
  buf and_7 (and_7_out, not_2_out);  // AND_Gate
  buf and_8 (and_8_out, in_2);  // AND_Gate
  buf and_9 (and_9_out, not_3_out);  // AND_Gate
  and and_10 (and_10_out, in_4, in_4);
  and and_11 (and_11_out, in_3, not_4_out);
  and and_12 (and_12_out, in_2, in_4, not_3_out, not_3_out);
  and and_13 (and_13_out, not_2_out, in_3);
  and and_14 (and_14_out, in_2, not_4_out);
  and and_15 (and_15_out, in_2, not_3_out);
  or c0 (c0_out, and_1_out, and_2_out, and_3_out, and_4_out);
  or c1 (c1_out, and_5_out, and_6_out, and_7_out);
  or c2 (c2_out, and_8_out, and_9_out, and_10_out);
  or c3 (c3_out, and_4_out, and_11_out, and_12_out, and_13_out);
  or c4 (c4_out, and_4_out, and_11_out);
  or c5 (c5_out, and_1_out, and_5_out, and_14_out, and_15_out);
  or c6 (c6_out, and_1_out, and_13_out, and_11_out, and_15_out);
  _7_Segment_Display u_7_segment_display_1 (
    .g(c6_out), .f(c5_out), .a(c0_out), .b(c1_out), .e(c4_out), .d(c3_out), .c(c2_out));  // open: dp
endmodule
