// Logisim project hw2_2.circ as structural Verilog
module main (
  input  in_1,
  input  in_2,
  input  in_3,
  input  in_4,
  input  in_5,
  input  in_6,
  input  in_7,
  input  in_8,
  input  in_9,
  input  in_10,
  input  in_11,
  input  in_12,
  output out_13,
  output out_14,
  output out_15,
  output out_16,
  output out_17,
  output out_18,
  output out_19,
  output out_20,
  output out_21,
  output out_22,
  output out_23,
  output out_24
);

  wire decoder_1_out0, decoder_1_out1, decoder_1_out3, decoder_1_out7, decoder_1_out12, decoder_1_out13,
       decoder_1_out14, decoder_1_out15, dx0, dx1, dx2, dx3, dx4, dx5, dx6, dx7;

  xor c3 (out_22, in_3, in_2, in_1, in_4);
  Decoder #(.select(4), .enable("false")) decoder_1 (
    .out0(decoder_1_out0), .out1(decoder_1_out1), .out2(dx0), .out3(decoder_1_out3), .out4(dx1), .out5(dx2),
    .out6(dx3), .out7(decoder_1_out7), .out8(dx4), .out9(dx5), .out10(dx6), .out11(dx7),
    .out12(decoder_1_out12), .out13(decoder_1_out13), .out14(decoder_1_out14), .out15(decoder_1_out15),
    .sel({out_22, out_24, out_21, out_23}));
  xor c2 (out_24, in_6, in_5, in_1, in_7);
  xor xor_1 (out_20, dx0, in_8);
  xor xor_2 (out_19, dx1, in_7);
  xor xor_3 (out_18, dx2, in_6);
  xor xor_4 (out_17, dx3, in_5);
  xor xor_5 (out_16, dx4, in_4);
  xor c1 (out_21, in_6, in_5, in_3, in_2, in_8);
  xor xor_6 (out_15, dx5, in_3);
  xor xor_7 (out_14, dx6, in_2);
  xor xor_8 (out_13, dx7, in_1);
  xor c0 (out_23, in_7, in_5, in_4, in_2, in_8);

  // Other names for the same wires on the sheet: cx0 = out_23; cx1 = out_21; cx2 = out_24; cx3 = out_22; c0 = in_12;
  //   c1 = in_11; c2 = in_10; c3 = in_9; d0 = in_8; d1 = in_7; d2 = in_6; d3 = in_5; d4 = in_4; d5 = in_3; d6 = in_2;
  //   d7 = in_1; z0 = out_20; z1 = out_19; z2 = out_18; z3 = out_17; z4 = out_16; z5 = out_15; z6 = out_14;
  //   z7 = out_13

  // Notes on the sheet:
  //   input
  //   output
endmodule
